// Logisim project m1_37069.circ as structural Verilog
module main (
  input  x,
  input  y,
  input  z,
  output Fxyz
);

  wire and_1_out, and_2_out, and_3_out, not_1_out, not_2_out, not_3_out;

  not not_1 (not_1_out, y);
  not not_2 (not_2_out, y);
  not not_3 (not_3_out, x);
  and and_1 (and_1_out, z, not_1_out, x);
  and and_2 (and_2_out, z, not_2_out, not_3_out);
  and and_3 (and_3_out, z, y, x);
  or or_1 (Fxyz, and_1_out, and_2_out, and_3_out);
endmodule

module NOT_NOR (
  input  x,
  output xNOT
);

  Pull_Resistor pull_resistor_1 (.node(xNOT));
  Transistor transistor_1 (.in(1'b1), .out(xNOT), .gate(x));
endmodule

module NOR_T (
  input  x,
  input  y,
  output xNORy
);

  wire transistor_1_out;

  Transistor transistor_1 (.in(1'b1), .out(transistor_1_out), .gate(x));
  Pull_Resistor pull_resistor_1 (.node(xNORy));
  Transistor transistor_2 (.in(transistor_1_out), .out(xNORy), .gate(y));
endmodule

module AND_NOR (
  input  x,
  input  y,
  output xANDy
);

  wire not_nor_1_xnot, not_nor_2_xnot, transistor_1_out;

  NOT_NOR not_nor_1 (.x(x), .xNOT(not_nor_1_xnot));
  Transistor transistor_1 (.in(1'b1), .out(transistor_1_out), .gate(not_nor_1_xnot));
  NOT_NOR not_nor_2 (.x(y), .xNOT(not_nor_2_xnot));
  Transistor transistor_2 (.in(transistor_1_out), .out(xANDy), .gate(not_nor_2_xnot));
  Pull_Resistor pull_resistor_1 (.node(xANDy));
endmodule

module OR_NOR (
  input  x,
  input  y,
  output xNORy
);

  wire pull_resistor_1_node, transistor_1_out;

  Transistor transistor_1 (.in(1'b1), .out(transistor_1_out), .gate(x));
  Pull_Resistor pull_resistor_1 (.node(pull_resistor_1_node));
  Transistor transistor_2 (.in(transistor_1_out), .out(pull_resistor_1_node), .gate(y));
  NOT_NOR not_nor_1 (.x(pull_resistor_1_node), .xNOT(xNORy));
endmodule

module XOR_SOP (
  input  x,
  input  y,
  output out_3
);

  wire not_nor_1_xnot, not_nor_2_xnot, pull_resistor_1_node, transistor_1_out, transistor_2_out,
       transistor_3_out;

  Transistor transistor_1 (.in(1'b1), .out(transistor_1_out), .gate(x));
  NOT_NOR not_nor_1 (.x(x), .xNOT(not_nor_1_xnot));
  Transistor transistor_2 (.in(1'b1), .out(transistor_2_out), .gate(not_nor_1_xnot));
  NOT_NOR not_nor_2 (.x(y), .xNOT(not_nor_2_xnot));
  Transistor transistor_3 (.in(transistor_2_out), .out(transistor_3_out), .gate(y));
  Pull_Resistor pull_resistor_1 (.node(pull_resistor_1_node));
  Transistor transistor_4 (.in(transistor_1_out), .out(pull_resistor_1_node), .gate(not_nor_2_xnot));
  Pull_Resistor pull_resistor_2 (.node(transistor_3_out));
  OR_NOR or_nor_1 (.x(pull_resistor_1_node), .y(transistor_3_out), .xNORy(out_3));
endmodule

module ODD3 (
  input  x,
  input  y,
  input  z,
  output ODDxyz
);

  wire and_1_out, and_2_out, and_3_out, and_4_out, not_1_out, not_2_out, not_3_out, not_4_out, not_5_out,
       not_6_out;

  not not_1 (not_1_out, z);
  not not_2 (not_2_out, y);
  not not_3 (not_3_out, z);
  not not_4 (not_4_out, x);
  not not_5 (not_5_out, y);
  not not_6 (not_6_out, x);
  and and_1 (and_1_out, not_1_out, not_2_out, x);
  and and_2 (and_2_out, not_3_out, y, not_4_out);
  and and_3 (and_3_out, z, not_5_out, not_6_out);
  and and_4 (and_4_out, z, y, x);
  or or_1 (ODDxyz, and_1_out, and_2_out, and_3_out, and_4_out);
endmodule

module PERSONAL_F (
  input  x,
  input  y,
  input  z,
  output Fxyz
);

  wire and_1_out, and_2_out, and_3_out, not_1_out, not_2_out, not_3_out;

  not not_1 (not_1_out, y);
  not not_2 (not_2_out, y);
  not not_3 (not_3_out, x);
  and and_1 (and_1_out, z, not_1_out, x);
  and and_2 (and_2_out, z, not_2_out, not_3_out);
  and and_3 (and_3_out, z, y, x);
  or or_1 (Fxyz, and_1_out, and_2_out, and_3_out);
endmodule
